// Digital circuit int_ctrl.dig as structural Verilog
module int_ctrl (
  input  INT1,
  input  INT0,
  output INTR,
  output out_2,
  output A0,
  output A1,
  output A2
);

  wire not_1_out, not_2_out;

  not not_1 (not_1_out, INT1);
  not not_2 (not_2_out, INT0);
  // _74ls148 _74ls148_1: pin names not known; wires that end beside it: 1'b1, 1'b1, 1'b1, 1'b1, 1'b1, 1'b1, not_1_out, not_2_out, 1'b0, 1'b1, 1'b0, INTR, out_2, A0, A1, A2
endmodule
